// Logisim project SixteenBitProzessor.circ as structural Verilog: 14 circuits, main circuit GatedMove
module EQU (
  input  I0,
  input  I1,
  output O0
);

  wire and_1_out, nor_1_out;

  and and_1 (and_1_out, I1, I0);
  nor nor_1 (nor_1_out, I0, I1);
  or or_1 (O0, and_1_out, nor_1_out);
endmodule

module GatedMove (
  input  Enable,
  input  I0,
  output Valid,
  output Q0
);

  wire not_1_out, or_1_out;

  not not_1 (not_1_out, Enable);
  and and_1 (Q0, Enable, I0);
  EQU Gleich (.I0(Q0), .I1(or_1_out), .O0(Valid));
  or or_1 (or_1_out, I0, not_1_out);
endmodule

module TestGatedMove (
  input  En_in,
  input  I0,
  output En_out,
  output O0
);

  GatedMove TestGatedMove (.Enable(En_in), .I0(I0), .Valid(En_out), .Q0(O0));
endmodule

module DualRailNAND (
  input  A,
  input  B,
  input  A_En,
  input  B_En,
  output Out0,
  output OutValid
);

  wire and_1_out, nand_1_out;

  nand nand_1 (nand_1_out, A, B);
  and and_1 (and_1_out, A_En, B_En);
  GatedMove gatedmove_1 (.Enable(nand_1_out), .I0(and_1_out), .Valid(Out0), .Q0(OutValid));
endmodule

module EightGatedMove (
  input  EnIn,
  input  [7:0] In0To8,
  output EnOut,
  output [7:0] Out0To8
);

  wire gatedmove_1_valid, gatedmove_2_valid, gatedmove_3_valid, gatedmove_4_valid, gatedmove_5_valid,
       gatedmove_6_valid, gatedmove_7_valid, gatedmove_8_valid;

  GatedMove gatedmove_1 (.Enable(EnIn), .I0(In0To8[0]), .Valid(gatedmove_1_valid), .Q0(Out0To8[0]));
  GatedMove gatedmove_2 (.Enable(EnIn), .I0(In0To8[1]), .Valid(gatedmove_2_valid), .Q0(Out0To8[1]));
  GatedMove gatedmove_3 (.Enable(EnIn), .I0(In0To8[2]), .Valid(gatedmove_3_valid), .Q0(Out0To8[2]));
  GatedMove gatedmove_4 (.Enable(EnIn), .I0(In0To8[3]), .Valid(gatedmove_4_valid), .Q0(Out0To8[3]));
  GatedMove gatedmove_5 (.Enable(EnIn), .I0(In0To8[4]), .Valid(gatedmove_5_valid), .Q0(Out0To8[4]));
  GatedMove gatedmove_6 (.Enable(EnIn), .I0(In0To8[5]), .Valid(gatedmove_6_valid), .Q0(Out0To8[5]));
  GatedMove gatedmove_7 (.Enable(EnIn), .I0(In0To8[6]), .Valid(gatedmove_7_valid), .Q0(Out0To8[6]));
  GatedMove gatedmove_8 (.Enable(EnIn), .I0(In0To8[7]), .Valid(gatedmove_8_valid), .Q0(Out0To8[7]));
  and AOut (EnOut, gatedmove_1_valid, gatedmove_2_valid, gatedmove_3_valid, gatedmove_4_valid, gatedmove_5_valid, gatedmove_6_valid, gatedmove_7_valid, gatedmove_8_valid);
endmodule

module SixteenGatedMove (
  input  EnIn,
  input  [15:0] In0To16,
  output EnOut,
  output [15:0] Out0To16
);

  wire eightgatedmove_1_enout, eightgatedmove_2_enout;

  EightGatedMove eightgatedmove_1 (
    .EnIn(EnIn), .In0To8(In0To16[7:0]), .EnOut(eightgatedmove_1_enout), .Out0To8(Out0To16[7:0]));
  EightGatedMove eightgatedmove_2 (
    .EnIn(EnIn), .In0To8(In0To16[15:8]), .EnOut(eightgatedmove_2_enout), .Out0To8(Out0To16[15:8]));
  and AndEn (EnOut, eightgatedmove_1_enout, eightgatedmove_2_enout);
endmodule

module CPU16_Regs (
  input  ExecEn,
  input  CommitEn,
  input  [15:0] PC_in,
  input  [7:0] A_in,
  input  [15:0] ADDR_in,
  output ExecEnOut,
  output CommitEnOut,
  output [15:0] NPC_out,
  output [15:0] PC_out,
  output [7:0] A_out,
  output [15:0] ADDR_out
);

  wire eightgatedmove_1_enout, sixteengatedmove_1_enout, sixteengatedmove_2_enout;

  SixteenGatedMove sixteengatedmove_1 (
    .EnIn(ExecEn), .In0To16(PC_in), .EnOut(sixteengatedmove_1_enout), .Out0To16(PC_out));
  EightGatedMove eightgatedmove_1 (.EnIn(ExecEn), .In0To8(A_in), .EnOut(eightgatedmove_1_enout), .Out0To8(A_out));
  SixteenGatedMove sixteengatedmove_2 (
    .EnIn(ExecEn), .In0To16(ADDR_in), .EnOut(sixteengatedmove_2_enout), .Out0To16(ADDR_out));
  SixteenGatedMove sixteengatedmove_3 (.EnIn(CommitEn), .In0To16(PC_out), .EnOut(CommitEnOut), .Out0To16(NPC_out));
  and AndOut (ExecEnOut, sixteengatedmove_1_enout, eightgatedmove_1_enout, sixteengatedmove_2_enout);
endmodule

module PCPlus1Bus16 (
  input  [15:0] PC_in,
  output [15:0] PCP1_Out
);

  Adder #(.width(16)) adder_1 (.a(PC_in), .b(16'h1), .out(PCP1_Out));  // open: cin, cout
endmodule

module EQ2_PC_NPC (
  input  [1:0] PC_in00to01,
  input  [1:0] NPC_in00to01,
  output EqPCNPC
);

  wire equ_1_o0, equ_2_o0;

  EQU equ_1 (.I0(NPC_in00to01[1]), .I1(PC_in00to01[0]), .O0(equ_1_o0));
  EQU equ_2 (.I0(PC_in00to01[1]), .I1(NPC_in00to01[0]), .O0(equ_2_o0));
  and and_1 (EqPCNPC, equ_1_o0, equ_2_o0);
endmodule

module Eq4_PC_NPC (
  input  [3:0] PC_in00to03,
  input  [3:0] NPC_in00to03,
  output EqPCNPC
);

  wire eq2_pc_npc_1_eqpcnpc, eq2_pc_npc_2_eqpcnpc;

  EQ2_PC_NPC eq2_pc_npc_1 (
    .PC_in00to01(NPC_in00to03[3:2]), .NPC_in00to01(PC_in00to03[1:0]), .EqPCNPC(eq2_pc_npc_1_eqpcnpc));
  EQ2_PC_NPC eq2_pc_npc_2 (
    .PC_in00to01(PC_in00to03[3:2]), .NPC_in00to01(NPC_in00to03[1:0]), .EqPCNPC(eq2_pc_npc_2_eqpcnpc));
  and and_1 (EqPCNPC, eq2_pc_npc_1_eqpcnpc, eq2_pc_npc_2_eqpcnpc);
endmodule

module Eq8_PC_NPC (
  input  [7:0] PC_in00to07,
  input  [7:0] NPC_in00to07,
  output EqPCNPC
);

  wire eq4_pc_npc_1_eqpcnpc, eq4_pc_npc_2_eqpcnpc;

  Eq4_PC_NPC eq4_pc_npc_1 (
    .PC_in00to03(NPC_in00to07[7:4]), .NPC_in00to03(PC_in00to07[3:0]), .EqPCNPC(eq4_pc_npc_1_eqpcnpc));
  Eq4_PC_NPC eq4_pc_npc_2 (
    .PC_in00to03(PC_in00to07[7:4]), .NPC_in00to03(NPC_in00to07[3:0]), .EqPCNPC(eq4_pc_npc_2_eqpcnpc));
  and and_1 (EqPCNPC, eq4_pc_npc_1_eqpcnpc, eq4_pc_npc_2_eqpcnpc);
endmodule

module Eq16_PC_NPC (
  input  [15:0] PC_in00to15,
  input  [15:0] NPC_in00to15,
  output EqPCNPC
);

  wire eq8_pc_npc_1_eqpcnpc, eq8_pc_npc_2_eqpcnpc;

  Eq8_PC_NPC eq8_pc_npc_1 (
    .PC_in00to07(NPC_in00to15[15:8]), .NPC_in00to07(PC_in00to15[7:0]), .EqPCNPC(eq8_pc_npc_1_eqpcnpc));
  Eq8_PC_NPC eq8_pc_npc_2 (
    .PC_in00to07(PC_in00to15[15:8]), .NPC_in00to07(NPC_in00to15[7:0]), .EqPCNPC(eq8_pc_npc_2_eqpcnpc));
  and and_1 (EqPCNPC, eq8_pc_npc_1_eqpcnpc, eq8_pc_npc_2_eqpcnpc);
endmodule

module Control16_Bus (
  input  STEP_CLOCK,
  input  EN,
  input  Reset,
  input  [15:0] PC,
  input  [15:0] NPC,
  output PHASE,
  output ExecEn,
  output CommitEn,
  output EqPCNPC
);

  wire eq16_eqpcnpc, not_1_out;

  D_Flip_Flop d_ff_1 (.D(not_1_out), .clk(STEP_CLOCK), .Q(PHASE), .reset(Reset));  // open: Qn, preset
  Eq16_PC_NPC eq16 (.PC_in00to15(PC), .NPC_in00to15(NPC), .EqPCNPC(eq16_eqpcnpc));
  not not_1 (not_1_out, PHASE);
  and and_1 (ExecEn, not_1_out, EN);
  and and_2 (CommitEn, EN, PHASE);
  and and_3 (EqPCNPC, PHASE, eq16_eqpcnpc);
endmodule

module CPU16_Main (
  input  PHASE,
  input  STEP_CLOCK,
  input  EN,
  input  ExecEn,
  input  Reset,
  input  CommitEn,
  input  EqPCNPC
);

  wire [7:0] undriven;
  wire [15:0] PCOut_Tunnel, PCP1Out_Tunnel, undriven_2;

  // Probe on PCOut_Tunnel
  // Probe on PCP1Out_Tunnel
  // Probe on undriven
  // Probe on undriven_2
  Control16_Bus control16_bus_1 (
    .STEP_CLOCK(STEP_CLOCK), .EN(EN), .Reset(Reset), .PC(PCOut_Tunnel), .NPC(PCP1Out_Tunnel), .PHASE(PHASE),
    .ExecEn(ExecEn), .CommitEn(CommitEn), .EqPCNPC(EqPCNPC));
  PCPlus1Bus16 pcplus1bus16_1 (.PC_in(PCOut_Tunnel), .PCP1_Out(PCP1Out_Tunnel));
  CPU16_Regs cpu16_regs_1 (
    .ExecEn(ExecEn), .CommitEn(CommitEn), .PC_in(PCOut_Tunnel), .A_in(undriven), .ADDR_in(undriven_2),
    .NPC_out(PCOut_Tunnel), .PC_out(PCOut_Tunnel));  // open: ExecEnOut, CommitEnOut, A_out, ADDR_out
  Adder #(.width(16)) adder_1 ();  // open: a, b, out, cin, cout
  SixteenGatedMove IR_Move16 ();  // open: EnIn, In0To16, EnOut, Out0To16
  SixteenGatedMove A_Move16 ();  // open: EnIn, In0To16, EnOut, Out0To16
  SixteenGatedMove AR_Move16 ();  // open: EnIn, In0To16, EnOut, Out0To16

  // Other names for the same wires on the sheet: CommitEnTunnel = CommitEn; ExecEnTunnel = ExecEn
endmodule
